# Fritzing sketch watering-system_schema (saved by Fritzing 0.9.3b)

parts:
  WeMos_D1_Mini1 = WeMos D1 Mini
  hc-sr1 = hc-sr04
  Součástka2 = IFR520 MOS module [package=THT]
  Součástka3 = FC-28 Soil Hygrometer Module
  MUX1 = 74HC4051 [package="DIP (Dual Inline) [THT]"]
  Součástka4 = IFR520 MOS module [package=THT]
  Součástka5 = FC-28 Soil Hygrometer Module
  Součástka6 = FC-28 Soil Hygrometer Module
  Součástka7 = FC-28 Soil Hygrometer Module
  M1 = DC Motor
  M2 = DC Motor
  WeMos_D1_Mini_OLED_Shield1 = WeMos D1 Mini OLED Shield
  Součástka8 = FC-28 Soil Hygrometer Module

nets:
  VCC: WeMos_D1_Mini1.3V3, Součástka2.VCC, Součástka3.VCC, MUX1.VDD, Součástka4.VCC, Součástka5.VCC, Součástka6.VCC, Součástka7.VCC, WeMos_D1_Mini_OLED_Shield1.3V3, Součástka8.VCC
  5V: WeMos_D1_Mini1.5V, hc-sr1.VCC
  N1: WeMos_D1_Mini1.A0, MUX1.IO
  N2: WeMos_D1_Mini1.D0, MUX1.C
  N3: WeMos_D1_Mini1.D1, WeMos_D1_Mini_OLED_Shield1.D2
  N4: WeMos_D1_Mini1.D2, WeMos_D1_Mini_OLED_Shield1.D1
  N5: WeMos_D1_Mini1.D3, hc-sr1.Echo
  N6: WeMos_D1_Mini1.D4, hc-sr1.Trig
  N7: WeMos_D1_Mini1.D5, MUX1.B
  N8: WeMos_D1_Mini1.D6, MUX1.A
  N9: WeMos_D1_Mini1.D7, Součástka2.SIG
  N10: WeMos_D1_Mini1.D8, Součástka4.SIG
  GND: WeMos_D1_Mini1.G, hc-sr1.GND, Součástka2.GND, Součástka3.GND, MUX1.INH, MUX1.VEE, MUX1.VSS, Součástka4.GND, Součástka5.GND, Součástka6.GND, Součástka7.GND, WeMos_D1_Mini_OLED_Shield1.G, Součástka8.GND
  N11: Součástka2.V+, M1.pin_1
  N12: Součástka2.V-, M1.pin_2
  N13: Součástka3.AO, MUX1.IO2
  N14: MUX1.IO4, Součástka8.AO
  N15: MUX1.IO3, Součástka5.AO
  N16: MUX1.IO0, Součástka6.AO
  N17: MUX1.IO1, Součástka7.AO
  N18: Součástka4.V+, M2.pin_1
  N19: Součástka4.V-, M2.pin_2

notes:
  TODO teplomer (D1, D2)

custom parts:
  FC-28 Soil Hygrometer Module: The FC-28 is a soil hygrometer module that uses the Texas Instruments LM393 comparator chip to provide an analog measurement of soil humidity. The digital output is high when soil moisture is over a certain threshold, as determined by adjusting the potentiometer.
  74HC4051: 8 channel analog multiplexer/demultiplexer
